// Logisim project Part 1.circ as structural Verilog: 1 circuit, main circuit main
module main (
  input  x,
  input  y,
  input  s,
  output f
);

  wire n7404_1_p2, n7408_1_p3, n7408_1_p6;

  // _7404 7404_1: pin names not known; wires that end beside it: s, n7404_1_p2
  // _7408 7408_1: pin names not known; wires that end beside it: x, n7404_1_p2, n7408_1_p3, s, y, n7408_1_p6
  // _7432 7432_1: pin names not known; wires that end beside it: n7408_1_p6, n7408_1_p3, f

  // Notes on the sheet:
  //   f =x&!s + y&s
endmodule
