// Logisim project Part 2.circ as structural Verilog: 1 circuit, main circuit main
module main (
  input  A,
  input  B,
  input  C,
  input  D,
  output f
);

  wire n7404_1_p2, n7404_1_p4, n7408_1_p3, n7408_1_p6;

  // _7404 7404_1: pin names not known; wires that end beside it: C, n7404_1_p2, B, n7404_1_p4
  // _7408 7408_1: pin names not known; wires that end beside it: A, n7404_1_p2, n7408_1_p3, n7404_1_p4, D, n7408_1_p6
  // _7432 7432_1: pin names not known; wires that end beside it: n7408_1_p3, n7408_1_p6, f

  // Notes on the sheet:
  //   f = a&!c+!b&d
endmodule
