// Logisim project draw2.circ as structural Verilog: 1 circuit, main circuit main
module main (
  input  A,
  input  B,
  input  C,
  input  D,
  output f
);

  wire and_1_out, and_2_out, not_1_out, not_2_out;

  not not_1 (not_1_out, B);
  not not_2 (not_2_out, C);
  and and_1 (and_1_out, A, not_2_out);
  and and_2 (and_2_out, not_1_out, D);
  or or_1 (f, and_1_out, and_2_out);

  // Notes on the sheet:
  //   f = a&!c+!b&d
endmodule
