// Logisim project part1.circ as structural Verilog: 1 circuit, main circuit main
module main (
  input  D,
  input  Clk,
  output Q_a__Q,
  output Q_b
);

  wire n7400_1_p3, n7400_1_p6, n7404_1_p2;

  // _7404 7404_1: pin names not known; wires that end beside it: D, n7404_1_p2
  // _7400 7400_1: pin names not known; wires that end beside it: D, Clk, n7400_1_p3, Clk, n7404_1_p2, n7400_1_p6, n7400_1_p3, Q_b, Q_a__Q, Q_a__Q, n7400_1_p6, Q_b

  // Notes on the sheet:
  //   Gated D Latch
  //   R
  //   S_g
  //   S
  //   R_g
endmodule
